# Fritzing sketch RCCarSketch (saved by Fritzing 0.9.3b)
breadboards: 1

parts:
  S1 = Pushbutton [package="[THT]"]
  S2 = Pushbutton [package="[THT]"]
  LED1 = LED - 5mm [color="Red (633nm)" package="5 mm [THT]"]
  LED2 = LED - 5mm [color="Red (633nm)" package="5 mm [THT]"]
  LED3 = LED - 5mm [color="Red (633nm)" package="5 mm [THT]"]
  LED4 = LED - 5mm [color="Red (633nm)" package="5 mm [THT]"]
  LED5 = LED - 5mm [color="Red (633nm)" package="5 mm [THT]"]
  LED6 = LED - 5mm [color="Red (633nm)" package="5 mm [THT]"]
  LED7 = LED - 5mm [color="Red (633nm)" package="5 mm [THT]"]
  LED8 = LED - 5mm [color="Red (633nm)" package="5 mm [THT]"]
  LED9 = LED - 5mm [color="Red (633nm)" package="5 mm [THT]"]
  LED10 = LED - 5mm [color="Red (633nm)" package="5 mm [THT]"]
  Part1 = Arduino Mega 2560 (Rev3)
  R1 = Resistor [tolerance=±5% resistance=220 package=THT]
  U1 = LIPO-110mAh [package=lipo-110]
  R2 = Resistor [tolerance=±5% resistance=100 package="0603 [SMD]"]
  R3 = Resistor [tolerance=±5% resistance=1k package="0603 [SMD]"]
  R4 = Resistor [tolerance=±5% resistance=1k package="0603 [SMD]"]
  LED11 = 7-SEGMENT-4DIGIT-YOUNGSUN [package=7-segment-4digit-youngsun-longpads]
  R5 = Resistor [tolerance=±5% resistance=1k package="0603 [SMD]"]
  R6 = Resistor [tolerance=±5% resistance=1k package="0603 [SMD]"]
  R7 = Resistor [tolerance=±5% resistance=1k package="0603 [SMD]"]
  Q1 = PNP-Transistor [package="TO92 [THT]"]
  Hall_Sensor_49e727bg = ACS712 [package=so08]
  LED12 = LED - 5mm [color="Red (633nm)" package="5 mm [THT]"]
  LED13 = LED - 5mm [color="Red (633nm)" package="5 mm [THT]"]  # not connected
  R8 = Resistor [tolerance=±5% resistance=100 package="0603 [SMD]"]
  Part2 = NRF24L01+ Breakout Board
  BAT1 = Battery Holders [package=battery-aa]
  BAT2 = Battery Holders [package=battery-aa]
  BAT3 = Battery Holders [package=battery-aa]

nets:
  N1: S1.Pin_1, S1.Pin_2, S2.Pin_1, S2.Pin_2, Part1.5V
  N2: S1.Pin_3, S1.Pin_4, Part1.D28, R4.Pin_1
  N3: S2.Pin_3, S2.Pin_4, Part1.D26, R3.Pin_1
  N4: LED1.cathode, LED2.cathode, LED3.cathode, LED4.cathode, LED5.cathode, LED6.cathode, LED7.cathode, LED8.cathode, LED9.cathode, LED10.cathode, R1.Pin_0
  N5: LED1.anode, Part1.D11_PWM
  N6: LED2.anode, Part1.D10_PWM
  N7: LED3.anode, Part1.D9_PWM
  N8: LED4.anode, Part1.D8_PWM
  N9: LED5.anode, Part1.D7_PWM
  N10: LED6.anode, Part1.D6_PWM
  N11: LED7.anode, Part1.D5_PWM
  N12: LED8.anode, Part1.D4_PWM
  N13: LED9.anode, Part1.D3_PWM
  N14: LED10.anode, Part1.D2_PWM
  N15: Part1.A1, R2.Pin_1
  GND: Part1.GND, R1.Pin_1, U1.-, R3.Pin_0, R4.Pin_0, Hall_Sensor_49e727bg.IP+, R8.Pin_1, Part2.GND
  N16: Part1.D13_PWM, Part2.CS
  N17: Part1.D12_PWM, Part2.CE
  3V3: Part1.3V3, Part1.D49, Hall_Sensor_49e727bg.IP-, Part2.VCC
  N18: Part1.D30, R5.Pin_0
  N19: Part1.D32, R6.Pin_0
  N20: Part1.D34, R7.Pin_0
  N21: Part1.D36, LED11.DIG4
  N22: Part1.D38, LED11.C
  N23: Part1.D40, LED11.APOS-C
  N24: Part1.D42, LED11.DIG3
  N25: Part1.D43, LED11.E
  N26: Part1.D44, LED11.COL-A
  N27: Part1.D45, LED11.DP
  N28: Part1.D46, LED11.D
  N29: Part1.D47, LED12.anode
  N30: Part1.D50, LED11.COL-C
  N31: U1.+, R2.Pin_0
  N32: LED11.APOS-A, R7.Pin_1
  N33: LED11.F, R6.Pin_1
  N34: LED11.A, R5.Pin_1
  N35: Q1.E, Hall_Sensor_49e727bg.VOUT
  N36: Q1.B, Hall_Sensor_49e727bg.GND
  N37: Q1.C, Hall_Sensor_49e727bg.FILT
  N38: LED12.cathode, R8.Pin_0
  N39: BAT1.-, BAT2.-, BAT3.-
  N40: BAT1.+, BAT2.+, BAT3.+

notes:
  G = 2
  + = 3
  Do = 4
  Brakelights

// code stored in the sketch: accel.ino
/*void Acceleration() {
  Serial.println("Acceleration");
  delay(1000);
  }
*//*
  #include "Wire.h"
  #include "elapsedMillis.h"

  #define    MPU9250_ADDRESS            0x68
  #define    MAG_ADDRESS                0x0C

  #define    GYRO_FULL_SCALE_250_DPS    0x00
  #define    GYRO_FULL_SCALE_500_DPS    0x08
  #define    GYRO_FULL_SCALE_1000_DPS   0x10
  #define    GYRO_FULL_SCALE_2000_DPS   0x18

  #define    ACC_FULL_SCALE_2_G        0x00
  #define    ACC_FULL_SCALE_4_G        0x08
  #define    ACC_FULL_SCALE_8_G        0x10
  #define    ACC_FULL_SCALE_16_G       0x18

  float acc;
  float acc2;
  float matka;
  elapsedMillis elapsedmil;
*/
/*
void I2Cread(uint8_t, uint8_t, uint8_t, uint8_t*);
void I2CwriteByte(uint8_t, uint8_t, uint8_t);
void accelerationSetup(void);
void accelerationLoop(void);

void I2Cread(uint8_t Address, uint8_t Register, uint8_t Nbytes, uint8_t* Data) {
  // Set register address
  Wire.beginTransmission(Address);
  Wire.write(Register);
  Wire.endTransmission();

  // Read Nbytes
  Wire.requestFrom(Address, Nbytes);
  uint8_t index = 0;
  while (Wire.available())
    Data[index++] = Wire.read();
}


// Write a byte (Data) in device (Address) at register (Register)
void I2CwriteByte(uint8_t Address, uint8_t Register, uint8_t Data) {
  // Set register address
  Wire.beginTransmission(Address);
  Wire.write(Register);
  Wire.write(Data);
  Wire.endTransmission();
}



void accelerationSetup() {
  Serial.println("Acc setup");
  // Arduino initializations
  Wire.begin();
  //Serial.begin(115200);
  //Serial.begin(9600);

  // Configure gyroscope range
  I2CwriteByte(MPU9250_ADDRESS, 27, GYRO_FULL_SCALE_2000_DPS);
  // Configure accelerometers range
  I2CwriteByte(MPU9250_ADDRESS, 28, ACC_FULL_SCALE_16_G);
  // Set by pass mode for the magnetometers
  I2CwriteByte(MPU9250_ADDRESS, 0x37, 0x02);

  // Request first magnetometer single measurement
  I2CwriteByte(MAG_ADDRESS, 0x0A, 0x01);
}

long int cpt = 0;

void accelerationLoop() {
  // put your main code here, to run repeatedly:
  Serial.println("Acc loop start");
  unsigned long StartTime;
  unsigned long CurrentTime;
  unsigned long ElapsedTime;

  // Read accelerometer and gyroscope
  uint8_t Buf[14];
  I2Cread(MPU9250_ADDRESS, 0x3B, 14, Buf);


  // Create 16 bits values from 8 bits data

  // Accelerometer
  int16_t ax = -(Buf[0] << 8 | Buf[1]);
  int16_t ay = -(Buf[2] << 8 | Buf[3]);
  int16_t az = Buf[4] << 8 | Buf[5];

  // Gyroscope
  int16_t gx = -(Buf[8] << 8 | Buf[9]);
  int16_t gy = -(Buf[10] << 8 | Buf[11]);
  int16_t gz = Buf[12] << 8 | Buf[13];

  if (ax <= -200 || ax >= 200)
  {
    acc = ax * 0.001 * 9.8;
  }

  //if (acc != acc2)
  //{
  if ((millis() - delayTimeAcc) > 250) {
    acc2 = acc;
    Serial.print(" Acc = ");
    Serial.print(acc, 2);
    Serial.print(" m/s2 ");
    Serial.println("");
    //}
    delayTimeAcc = millis();
    //delay(250);
  }
}
*/

// code stored in the sketch: Lights.ino
void Led() {

  //Serial.println("Led start");
  if ((millis() - delayTime) > 80) { //timer = 20, 0.02sec
    if (count2 < 12) {
      count2++;
      digitalWrite(pinArray[count2], HIGH);

      if (count2 > 2) {
        digitalWrite(pinArray[count2 - 3], LOW);
      }
    }
    if (count2 > 11) {

      count3--;
      digitalWrite(pinArray[count3], HIGH);

      if (count3 < 10) {
        digitalWrite(pinArray[count3 + 3], LOW);
      }
    }
    delayTime = millis();
  }

  if (count2 == 12 && count3 == -3) { //led loop
    count2 = -1;
    count3 = 12;
  }

}   //Led() end

void LedOff() {

  Serial.println("LedOff start");
  for (int i = 0; i < 10; i++)
    digitalWrite(pinArray[i], LOW);

}

// code stored in the sketch: main.ino
#include "Wire.h"
#include "elapsedMillis.h"
#include "SevSeg.h"

//Nrf
#include <SPI.h>
#include "RF24.h"

// nopeus

//calculations
//tire radius ~ 1,9685 inches
//circumference = pi*2*r =~85 inches
//max speed of 35mph =~ 616inches/second
//max rps =~7.25

#define reed 49 //pin connected to read switch

//storage variables
float radius = 1.968;// tire radius (in inches)- CHANGE THIS FOR YOUR OWN BIKE

int reedVal;
long timer = 0;// time between one full rotation (in ms)
float mph = 0.00;
float mph2 = 0.00;
float mph3 = 0.00;
float circumference;
boolean backlight;

int maxReedCounter = 50;//min time (in ms) of one rotation (for debouncing)
int reedCounter;

int switchState = 0;
// nopeus

/****************** User Config ***************************/
/***      Set this radio as radio number 0 or 1         ***/
bool radioNumber = 0;

/* Hardware configuration: Set up nRF24L01 radio on SPI bus plus pins 7 & 8 */
RF24 radio(12, 13);
/**********************************************************/

byte addresses[][6] = {"1Node", "2Node"};

// Used to control whether this node is sending or receiving
bool role = 0;
//Nrf

/*
  #define    MPU9250_ADDRESS            0x68
  #define    MAG_ADDRESS                0x0C

  #define    GYRO_FULL_SCALE_250_DPS    0x00
  #define    GYRO_FULL_SCALE_500_DPS    0x08
  #define    GYRO_FULL_SCALE_1000_DPS   0x10
  #define    GYRO_FULL_SCALE_2000_DPS   0x18

  #define    ACC_FULL_SCALE_2_G        0x00
  #define    ACC_FULL_SCALE_4_G        0x08
  #define    ACC_FULL_SCALE_8_G        0x10
  #define    ACC_FULL_SCALE_16_G       0x18
*/
//float acc;
//float acc2;
//float matka;
//elapsedMillis elapsedmil;


SevSeg sevseg; //Initiate a seven segment controller object
uint8_t d;
//Led
int pinArray[] = {2, 3, 4, 5, 6, 7, 8, 9, 10, 11};
int count = 0;
int count2 = -1;
int count3 = 12;
//int timer = 20;
long delayTime;
long SenddelayTime; //Send data
long delayTimeAcc;
long delayTimeVol;
long delayNopeus;
long delayTimeBrake;

float v1;
float kmh1;

//void accelerationSetup(void);
//void Voltage(void);
//void accelerationLoop(void);
uint8_t Off(uint8_t);

//Buttons
// constants won't change. They're used here to set pin numbers:
const int button26Pin = 26;     // the number of the pushbutton pin
const int button28Pin = 28;     // the number of the pushbutton pin

// variables will change:
int buttonState26 = 0;         // variable for reading the pushbutton status
int buttonState28 = 0;

byte oldbutton26 = 0;
byte oldbutton28 = 0;
byte state26 = 0;
byte state28 = 0;
byte pressed26 = 0;
byte pressed28 = 0;
//Buttons

void setup() {

  Serial.begin(115200);
  displaySetup();   //for voltage display

  //calibrationSetup();

  NopeusSetup();
  //voltage
  //Serial.begin(9600);

  //Buttons
  pinMode(button26Pin, INPUT);
  pinMode(button28Pin, INPUT);
  //Buttons

  //led
  for (count = 0; count < 10; count++) {
    pinMode(pinArray[count], OUTPUT);
  }

  //Nrf

  Serial.println(F("RF24/examples/GettingStarted"));
  Serial.println(F("*** PRESS 'T' to begin transmitting to the other node"));

  radio.begin();

  // Set the PA Level low to prevent power supply related issues since this is a
  // getting_started sketch, and the likelihood of close proximity of the devices. RF24_PA_MAX is default.
  radio.setPALevel(RF24_PA_LOW);

  // Open a writing and reading pipe on each radio, with opposite addresses
  if (radioNumber) {
    radio.openWritingPipe(addresses[1]);
    radio.openReadingPipe(1, addresses[0]);
  } else {
    radio.openWritingPipe(addresses[0]);
    radio.openReadingPipe(1, addresses[1]);
  }

  // Start the radio listening for data
  radio.startListening();
  //Nrf

  //Acceleration
  //  accelerationSetup();

}   //setup() end

//int res = Voltage(res);

void loop() {
  //int res = Voltage(res);
  //int luku;
  //displayLoop();
  //Nrf
  NopeusLoop();
  /****************** Ping Out Role ***************************/

  if (role == 0)  {
    if ((millis() - SenddelayTime) > 1000) {
      radio.stopListening();                                    // First, stop listening so we can talk.

      //v1 = displayLoop(v1); //get voltage
      kmh1 = getKMH(kmh1);
      //Serial.print("V1 : ");
      //Serial.println(v1);

      Serial.println(F("Now sending"));
      
      //unsigned long start_time = micros();                             // Take the time, and send it.  This will block until complete

      if (!radio.write( &kmh1, sizeof(float) )) {
        Serial.println(F("failed"));
      }


      radio.startListening();                                    // Now, continue listening

      unsigned long started_waiting_at = millis();               // Set up a timeout period, get the current microseconds
      boolean timeout = false;                                   // Set up a variable to indicate if a response was received or not

      while ( ! radio.available() ) {                            // While nothing is received
        if (millis() - started_waiting_at > 200 ) {           // If waited longer than 200ms, indicate timeout and exit while loop
          timeout = true;
          break;
        }
      }
      /*
            if ( timeout ) {                                            // Describe the results
              Serial.println(F("Failed, response timed out."));
            } else {
              //unsigned long got_time;                                // Grab the response, compare, and send to debugging spew
              float got_value;
              radio.read( &got_value, sizeof(float) );
              //unsigned long end_time = micros();

              // Spew it
              Serial.print(F("Sent "));
              Serial.print(kmh1);
              Serial.print(F(", Got response "));
              Serial.println(got_value);

            }
      */
      SenddelayTime = millis();
    }
  }



  /****************** Pong Back Role ***************************/
  /*
    if ( role == 0 )
    {
      unsigned long got_value;

      if ( radio.available()) {
        // Variable for the received timestamp
        while (radio.available()) {                                   // While there is data ready
          radio.read( &got_value, sizeof(unsigned long) );             // Get the payload
        }

        radio.stopListening();                                        // First, stop listening so we can talk
        radio.write( &got_value, sizeof(unsigned long) );              // Send the final one back.
        radio.startListening();                                       // Now, resume listening so we catch the next packets.
        Serial.print(F("Sent response "));
        Serial.println(got_value);
      }
    }


  */

  /****************** Change Roles via Serial Commands ***************************/
  /*
    if ( Serial.available() )
    {
      char c = toupper(Serial.read());
      if ( c == 'T' && role == 0 ) {
        Serial.println(F("*** CHANGING TO TRANSMIT ROLE -- PRESS 'R' TO SWITCH BACK"));
        role = 1;                  // Become the primary transmitter (ping out)

      } else if ( c == 'R' && role == 1 ) {
        Serial.println(F("*** CHANGING TO RECEIVE ROLE -- PRESS 'T' TO SWITCH BACK"));
        role = 0;                // Become the primary receiver (pong back)
        radio.startListening();

      }
    }

  */
  //Nrf

  //Buttons
  // read the state of the pushbutton value:

  buttonState26 = digitalRead(button26Pin);
  buttonState28 = digitalRead(button28Pin);

  // check if the pushbutton is pressed. If it is, the buttonState is HIGH:

  if (buttonState26 == LOW) {
    pressed26 = 0;
  }

  //Button26
  if (buttonState26 == HIGH && !oldbutton26 && !pressed26) {

    if (state26 == 0)
    {
      Serial.println("Button26 On");
      state26 = 1;
      //while (buttonState26 == HIGH) {Led();}


    }
    else
    {
      state26 = 0;
    }
    oldbutton26 = 1;
    pressed26 = 1;

  } else if (buttonState26 == HIGH && oldbutton26 && !pressed26) {

    if (state26 == 1)
    {
      Serial.println("Button26 Off");
      state26 = 0;
      LedOff();
      role = 0;
    }
    else
    {
      state26 = 1;
    }
    oldbutton26 = 0;
    pressed26 = 1;
  } //Button26

  if (buttonState28 == LOW) {
    //Serial.println("28 low");
    pressed28 = 0;
  }

  //Button28
  if (buttonState28 == HIGH && !oldbutton28 && !pressed28) {

    if (state28 == 0)
    {
      Serial.println("Button28 On");
      displayLoop();
      state28 = 1;
      role = 1; //send off
    }
    else
    {
      state28 = 0;
    }
    oldbutton28 = 1;
    pressed28 = 1;

  } else if (buttonState28 == HIGH && oldbutton28 && !pressed28) {

    if (state28 == 1)
    {
      Serial.println("Button28 Off"); //display off
      displayOff();
      role = 0; //send on
      state28 = 0;
    }
    else
    {
      state28 = 1;
    }
    oldbutton28 = 0;
    pressed28 = 1;
  } //Button28

  if (buttonState26 == LOW && state26) {
    Led();
    role = 1; //send off

  }
  if (buttonState28 == LOW && state28) {
    displayLoop();
    role = 1; //send off
  }
  //Buttons

}   //loop() end

// code stored in the sketch: nopeus.ino
//bike speedometer
//by Amanda Ghassaei 2012
//https://www.instructables.com/id/Arduino-Bike-Speedometer/

/*
   This program is free software; you can redistribute it and/or modify
   it under the terms of the GNU General Public License as published by
   the Free Software Foundation; either version 3 of the License, or
   (at your option) any later version.

*/

//calculations
//tire radius ~ 1,9685 inches
//circumference = pi*2*r =~85 inches
//max speed of 35mph =~ 616inches/second
//max rps =~7.25

void NopeusSetup() {

  reedCounter = maxReedCounter;
  circumference = 2 * 3.141593 * radius;
  //pinMode(1, OUTPUT); //tx, display?
  pinMode(reed, INPUT);
  pinMode(47, OUTPUT); //Led

  // TIMER SETUP- the timer interrupt allows preceise timed measurements of the reed switch
  //for mor info about configuration of arduino timers see http://arduino.cc/playground/Code/Timer1
  cli();//stop interrupts

  //set timer1 interrupt at 1kHz
  TCCR1A = 0;// set entire TCCR1A register to 0
  TCCR1B = 0;// same for TCCR1B
  TCNT1  = 0;
  // set timer count for 1khz increments
  OCR1A = 1999;// = (1/1000) / ((1/(16*10^6))*8) - 1
  // turn on CTC mode
  TCCR1B |= (1 << WGM12);
  // Set CS11 bit for 8 prescaler
  TCCR1B |= (1 << CS11);
  // enable timer compare interrupt
  TIMSK1 |= (1 << OCIE1A);

  sei();//allow interrupts
  //END TIMER SETUP

  //Serial.begin(9600);
}


ISR(TIMER1_COMPA_vect) {//Interrupt at freq of 1kHz to measure reed switch
  reedVal = digitalRead(reed);//get val of A0
  if (reedVal) { //if reed switch is closed
    if (reedCounter == 0) { //min time between pulses has passed
      mph = (91.4 * float(circumference)) / float(timer); //calculate miles per hour
      timer = 0;//reset timer
      reedCounter = maxReedCounter;//reset reedCounter
    }
    else {
      if (reedCounter > 0) { //don't let reedCounter go negative
        reedCounter -= 1;//decrement reedCounter
      }
    }
  }
  else { //if reed switch is open
    if (reedCounter > 0) { //don't let reedCounter go negative
      reedCounter -= 1;//decrement reedCounter
    }
  }
  if (timer > 100) {
    mph = 0;//if no new pulses from reed switch- tire is still, set mph to 0
  }
  else {
    timer += 1;//increment timer
  }
}
float getKMH (float kmh)
{
  kmh = mph;
  return kmh;
}

void displayMPH() {

  Serial.write(12);//clear
  Serial.write("Speed = ");
  Serial.write(13);//start a new line
  Serial.print(mph);
  Serial.println(" km/h ");
  //Serial.write("0.00 MPH ");
}
//getKMH(kmh)
//Serial.print("Vauhti : ");
//Serial.println(getKMH(kmh1));


void NopeusLoop() {

  //print mph once a second
  if ((millis() - delayNopeus) > 1000) {
    displayMPH();
    delayNopeus = millis();
  }
  digitalWrite(47, LOW);
  //Serial.println(mph);
  //Serial.println(mph2);
  //mph3 = mph;
  if (mph < mph2) {

    Serial.println ("pienenee");

    if ((millis() - delayTimeBrake) > 1000) {

      digitalWrite(47, HIGH);
      delayTimeBrake = millis();

    }
  }

  mph2 = mph;

}

// code stored in the sketch: Off.ino
uint8_t OffName(uint8_t d, char nimi[]) {
  Serial.println("Off start");
  while (Serial.available()) {

    uint8_t k;
    k = Serial.read();

    if ( k == 'x' ) {
      Serial.print(nimi);
      Serial.println(" off ");
      d = 'x';
      //LedOff();   //Turn off 2 last led
      displayOff();
      //return d;
      break;
    }
    //return d;
  }
  return d;
}

// code stored in the sketch: Voltage.ino
void displaySetup() {
  Serial.println("display setup");
  byte numDigits = 4;
  byte digitPins[] = {30, 32, 34, 36};
  byte segmentPins[] = {38, 40, 42, 44, 46, 48, 45, 43};
  sevseg.begin(COMMON_CATHODE, numDigits, digitPins, segmentPins);
  sevseg.setBrightness(90);

}

void displayOff() {
  Serial.println("display off");
  sevseg.blank();
  
  //byte hardwareConfig = 3;
  //sevseg.begin(hardwareConfig, numDigits, digitPins);
  
  //sevseg.setNumber(0000, 0);
  //sevseg.refreshDisplay(); // Must run repeatedly
  //sevseg.setBrightness(0);
  //sevseg.refreshDisplay();
}

/*
  int Voltage(int result) {

  int sensorValue = analogRead(A1);
  float voltage = sensorValue * (5.0 / 1023.0);
  result = voltage;
  Serial.println(voltage);
  delay(500);
  return result;

  }
*/
//int result = 1245;
void displayLoop() {
  //Serial.println("Voltage loop start");
  int sensorValue = analogRead(A1);
  float voltage = sensorValue * (5.0 / 1023.0);
  v1 = voltage;
  
  //if ((millis() - delayTimeVol) > 1000) { //timer = 1000, 1.00sec
    //Serial.print("Voltage : ");
    //Serial.println(voltage);
    //while not (radio.available(0))
    //{
    //radio.write(&voltage, sizeof(voltage));
    //}
    //delayTimeVol = millis();
  //}

  //kmh1 = getKMH();
  sevseg.setNumber(kmh1, 3);
  Serial.print("Nopeus : ");
  Serial.println(kmh1);
  sevseg.refreshDisplay(); // Must run repeatedly
  //return v1;
}
